# Fritzing sketch ATtinyModule (saved by Fritzing 0.9.3b)
breadboards: 2

parts:
  Part1 = Arduino Pro Mini v13
  U1 = RS485 [package=so08]
  U2 = RS485 [package=so08]
  U3 = attiny85 [package=dip]
  R1 = Rotary Potentiometer (Small) [maximum_resistance=100kΩ package=THT]
  J1 = Generic female header - 7 pins [form="♀ (female)" package=THT]

nets:
  GND: Part1.GND, U1._RE, U1.DE, U1.GND, U2.GND, U3.Pin_4, R1.leg2, J1.GND
  VCC: Part1.VCC, U1.VCC, U2._RE, U2.DE, U2.VCC, U3.Pin_8, R1.leg1, J1.VDD
  N1: Part1.D13/SCK, J1.SCK
  N2: Part1.D11_PWM/MOSI, J1.SDA
  N3: Part1.D10_PWM/SS, J1.CS
  N4: Part1.D9_PWM, J1.RES
  N5: Part1.D8, J1.DC
  N6: Part1.D1/RX, U1.RO
  N7: U1.A, U2.A
  N8: U1.B, U2.B
  N9: U2.DI, U3.Pin_5
  N10: U3.Pin_7, R1.wiper

custom parts:
  Generic female header - 7 pins: Generic female header
