# Fritzing sketch MonitorHall (saved by Fritzing 0.9.3b)
breadboards: 2

parts:
  Part1 = Arduino Pro Mini v13
  U1 = RS485 [package=so08]
  U2 = RS485 [package=so08]
  U3 = attiny85 [package=dip]
  J1 = female pin header, 3 pins [form="♀ (female)"]
  OH137 = female pin header, 3 pins [form="♀ (female)"]

nets:
  VCC: Part1.VCC, U1.VCC, U2._RE, U2.DE, U2.VCC, U3.Pin_8, J1.pin1, OH137.pin1
  GND: Part1.GND, U1._RE, U1.DE, U1.GND, U2.GND, U3.Pin_4, J1.pin2, OH137.pin2
  N1: Part1.D3_PWM, U1.RO
  N2: U1.A, U2.A
  N3: U1.B, U2.B
  N4: U2.DI, U3.Pin_5
  N5: U3.Pin_2, OH137.pin3
  N6: U3.Pin_3, J1.pin3
