# Fritzing sketch MotorTest (saved by Fritzing 0.9.3b)
circuit board: 6.1cm x 4.6cm
breadboards: 1

parts:
  DPDT_Relay2 = DPDT Relay [chip_label=Relay package="DIP (Dual Inline) [THT]"]
  DPDT_Relay4 = DPDT Relay [chip_label=Relay package="DIP (Dual Inline) [THT]"]
  DPDT_Relay5 = DPDT Relay [chip_label=Relay package="DIP (Dual Inline) [THT]"]
  DPDT_Relay6 = DPDT Relay [chip_label=Relay package="DIP (Dual Inline) [THT]"]
  J1 = female pin header, 1 pin [form="♀ (female)"]
  J2 = female pin header, 1 pin [form="♀ (female)"]
  J3 = female pin header, 1 pin [form="♀ (female)"]
  J4 = female pin header, 1 pin [form="♀ (female)"]
  J5 = female pin header, 1 pin [form="♀ (female)"]
  J7 = female pin header, 1 pin [form="♀ (female)"]
  J8 = female pin header, 1 pin [form="♀ (female)"]
  J9 = female pin header, 1 pin [form="♀ (female)"]
  J10 = female pin header, 1 pin [form="♀ (female)"]
  J11 = female pin header, 1 pin [form="♀ (female)"]
  J12 = female pin header, 1 pin [form="♀ (female)"]
  J13 = female pin header, 1 pin [form="♀ (female)"]
  J14 = female pin header, 1 pin [form="♀ (female)"]
  DPDT_Relay1 = DPDT Relay [chip_label=Relay package="DIP (Dual Inline) [THT]"]
  D1 = Rectifier Diode [part_number=1N4001 package="300 mil [THT]"]
  D2 = Rectifier Diode [part_number=1N4001 package="300 mil [THT]"]
  D3 = Rectifier Diode [part_number=1N4001 package="300 mil [THT]"]
  D4 = Rectifier Diode [part_number=1N4001 package="300 mil [THT]"]
  D5 = Rectifier Diode [part_number=1N4001 package="300 mil [THT]"]
  D6 = Rectifier Diode [part_number=1N4001 package="300 mil [THT]"]
  Q1 = NPN-Transistor [package="TO92 [THT]"]
  R1 = Resistor [tolerance=±5% resistance=10k package=THT]
  Q2 = NPN-Transistor [package="TO92 [THT]"]
  Q3 = NPN-Transistor [package="TO92 [THT]"]
  Q4 = NPN-Transistor [package="TO92 [THT]"]
  Q5 = NPN-Transistor [package="TO92 [THT]"]
  Q6 = NPN-Transistor [package="TO92 [THT]"]
  R2 = Resistor [tolerance=±5% resistance=10k package=THT]
  R3 = Resistor [tolerance=±5% resistance=10k package=THT]
  R4 = Resistor [tolerance=±5% resistance=10k package=THT]
  R5 = Resistor [tolerance=±5% resistance=10k package=THT]
  R6 = Resistor [tolerance=±5% resistance=10k package=THT]
  DPDT_Relay3 = DPDT Relay [chip_label=Relay package="DIP (Dual Inline) [THT]"]
  J6 = female pin header, 1 pin [form="♀ (female)"]
  J15 = female pin header, 1 pin [form="♀ (female)"]
  J16 = female pin header, 1 pin [form="♀ (female)"]
  R7 = Resistor [tolerance=±5% resistance=1k package=THT]
  J17 = female pin header, 1 pin [form="♀ (female)"]
  R8 = Resistor [tolerance=±5% resistance=1k package=THT]
  J18 = female pin header, 1 pin [form="♀ (female)"]
  J19 = female pin header, 1 pin [form="♀ (female)"]
  J20 = female pin header, 1 pin [form="♀ (female)"]
  J21 = female pin header, 1 pin [form="♀ (female)"]
  J22 = female pin header, 1 pin [form="♀ (female)"]
  J23 = female pin header, 1 pin [form="♀ (female)"]
  J24 = female pin header, 1 pin [form="♀ (female)"]
  J25 = female pin header, 1 pin [form="♀ (female)"]
  J26 = female pin header, 1 pin [form="♀ (female)"]
  J27 = female pin header, 1 pin [form="♀ (female)"]
  J28 = female pin header, 1 pin [form="♀ (female)"]
  J29 = female pin header, 1 pin [form="♀ (female)"]
  R9 = Resistor [tolerance=±5% resistance=1k package=THT]
  R10 = Resistor [tolerance=±5% resistance=1k package=THT]
  R11 = Resistor [tolerance=±5% resistance=1k package=THT]
  R12 = Resistor [tolerance=±5% resistance=1k package=THT]
  R13 = Resistor [tolerance=±5% resistance=1k package=THT]
  R14 = Resistor [tolerance=±5% resistance=1k package=THT]
  R15 = Resistor [tolerance=±5% resistance=1k package=THT]
  R16 = Resistor [tolerance=±5% resistance=1k package=THT]
  DPDT_Relay7 = DPDT Relay [chip_label=Relay package="DIP (Dual Inline) [THT]"]
  Q8 = PNP-Transistor [package="TO92 [THT]"]
  R17 = Resistor [tolerance=±5% resistance=10k package=THT]
  Q10 = NPN-Transistor [package="TO92 [THT]"]
  R18 = Resistor [tolerance=±5% resistance=10k package=THT]
  R19 = Resistor [tolerance=±5% resistance=10k package=THT]
  IN = female pin header, 1 pin [form="♀ (female)"]
  Out = female pin header, 1 pin [form="♀ (female)"]
  IN1 = female pin header, 1 pin [form="♀ (female)"]
  IN2 = female pin header, 1 pin [form="♀ (female)"]
  Q11 = PNP-Transistor [package="TO92 [THT]"]
  Q12 = NPN-Transistor [package="TO92 [THT]"]
  R20 = Resistor [tolerance=±5% resistance=10k package=THT]
  R21 = Resistor [tolerance=±5% resistance=10k package=THT]
  R22 = Resistor [tolerance=±5% resistance=10k package=THT]
  IN3 = female pin header, 1 pin [form="♀ (female)"]
  IN4 = female pin header, 1 pin [form="♀ (female)"]
  Out1 = female pin header, 1 pin [form="♀ (female)"]
  IN5 = female pin header, 1 pin [form="♀ (female)"]
  D7 = Rectifier Diode [part_number=1N4001 package="300 mil [THT]"]
  Q13 = NPN-Transistor [package="TO92 [THT]"]
  R23 = Resistor [tolerance=±5% resistance=10k package=THT]
  Out2 = female pin header, 1 pin [form="♀ (female)"]
  DPDT_Relay8 = DPDT Relay [chip_label=Relay package="DIP (Dual Inline) [THT]"]
  IN6 = female pin header, 1 pin [form="♀ (female)"]
  IN7 = female pin header, 1 pin [form="♀ (female)"]
  IN8 = female pin header, 1 pin [form="♀ (female)"]
  Out3 = female pin header, 1 pin [form="♀ (female)"]
  Out4 = female pin header, 1 pin [form="♀ (female)"]
  IN9 = female pin header, 1 pin [form="♀ (female)"]
  IN10 = female pin header, 1 pin [form="♀ (female)"]
  IN11 = female pin header, 1 pin [form="♀ (female)"]
  Out5 = female pin header, 1 pin [form="♀ (female)"]
  D8 = Rectifier Diode [part_number=1N4001 package="300 mil [THT]"]
  Q14 = NPN-Transistor [package="TO92 [THT]"]
  R24 = Resistor [tolerance=±5% resistance=10k package=THT]
  R25 = Resistor [tolerance=±5% resistance=10k package=THT]
  R26 = Resistor [tolerance=±5% resistance=10k package=THT]
  R27 = Resistor [tolerance=±5% resistance=10k package=THT]
  R28 = Resistor [tolerance=±5% resistance=10k package=THT]
  R29 = Resistor [tolerance=±5% resistance=10k package=THT]
  R30 = Resistor [tolerance=±5% resistance=10k package=THT]
  Q15 = PNP-Transistor [package="TO92 [THT]"]
  Q16 = PNP-Transistor [package="TO92 [THT]"]
  Q17 = NPN-Transistor [package="TO92 [THT]"]
  Q18 = NPN-Transistor [package="TO92 [THT]"]
  DPDT_Relay9 = DPDT Relay [chip_label=Relay package="DIP (Dual Inline) [THT]"]
  IN13 = female pin header, 1 pin [form="♀ (female)"]
  IN14 = female pin header, 1 pin [form="♀ (female)"]
  Out6 = female pin header, 1 pin [form="♀ (female)"]
  Out7 = female pin header, 1 pin [form="♀ (female)"]
  IN15 = female pin header, 1 pin [form="♀ (female)"]
  D9 = Rectifier Diode [part_number=1N4001 package="300 mil [THT]"]
  Q19 = NPN-Transistor [package="TO92 [THT]"]
  R32 = Resistor [tolerance=±5% resistance=10k package=THT]
  R33 = Resistor [tolerance=±5% resistance=10k package=THT]
  R34 = Resistor [tolerance=±5% resistance=10k package=THT]
  R37 = Resistor [tolerance=±5% resistance=10k package=THT]
  Q21 = PNP-Transistor [package="TO92 [THT]"]
  Q22 = NPN-Transistor [package="TO92 [THT]"]
  5V = female pin header, 1 pin [form="♀ (female)"]
  12v = female pin header, 1 pin [form="♀ (female)"]
  GND = female pin header, 1 pin [form="♀ (female)"]
  Q24 = PNP-Transistor [package="TO92 [THT]"]
  Q25 = PNP-Transistor [package="TO92 [THT]"]
  Q26 = NPN-Transistor [package="TO92 [THT]"]
  Q27 = NPN-Transistor [package="TO92 [THT]"]
  DPDT_Relay10 = DPDT Relay [chip_label=Relay package="DIP (Dual Inline) [THT]"]
  12v1 = female pin header, 1 pin [form="♀ (female)"]
  5V1 = female pin header, 1 pin [form="♀ (female)"]
  Out8 = female pin header, 1 pin [form="♀ (female)"]
  IN16 = female pin header, 1 pin [form="♀ (female)"]
  Out9 = female pin header, 1 pin [form="♀ (female)"]
  IN17 = female pin header, 1 pin [form="♀ (female)"]
  IN18 = female pin header, 1 pin [form="♀ (female)"]
  IN19 = female pin header, 1 pin [form="♀ (female)"]
  IN20 = female pin header, 1 pin [form="♀ (female)"]
  Out10 = female pin header, 1 pin [form="♀ (female)"]
  IN21 = female pin header, 1 pin [form="♀ (female)"]
  D10 = Rectifier Diode [part_number=1N4001 package="300 mil [THT]"]
  Q28 = NPN-Transistor [package="TO92 [THT]"]
  R38 = Resistor [tolerance=±5% resistance=10k package=THT]
  R39 = Resistor [tolerance=±5% resistance=10k package=THT]
  R40 = Resistor [tolerance=±5% resistance=10k package=THT]
  R41 = Resistor [tolerance=±5% resistance=10k package=THT]
  R42 = Resistor [tolerance=±5% resistance=10k package=THT]
  R43 = Resistor [tolerance=±5% resistance=10k package=THT]
  R44 = Resistor [tolerance=±5% resistance=10k package=THT]
  Q29 = PNP-Transistor [package="TO92 [THT]"]
  Q30 = PNP-Transistor [package="TO92 [THT]"]
  Q31 = NPN-Transistor [package="TO92 [THT]"]
  Q32 = NPN-Transistor [package="TO92 [THT]"]
  DPDT_Relay11 = DPDT Relay [chip_label=Relay package="DIP (Dual Inline) [THT]"]
  Out11 = female pin header, 1 pin [form="♀ (female)"]
  IN22 = female pin header, 1 pin [form="♀ (female)"]
  Out12 = female pin header, 1 pin [form="♀ (female)"]
  IN23 = female pin header, 1 pin [form="♀ (female)"]
  IN24 = female pin header, 1 pin [form="♀ (female)"]
  IN25 = female pin header, 1 pin [form="♀ (female)"]
  IN26 = female pin header, 1 pin [form="♀ (female)"]
  Out13 = female pin header, 1 pin [form="♀ (female)"]
  IN27 = female pin header, 1 pin [form="♀ (female)"]
  D11 = Rectifier Diode [part_number=1N4001 package="300 mil [THT]"]
  Q33 = NPN-Transistor [package="TO92 [THT]"]
  R45 = Resistor [tolerance=±5% resistance=10k package=THT]
  R46 = Resistor [tolerance=±5% resistance=10k package=THT]
  R47 = Resistor [tolerance=±5% resistance=10k package=THT]
  R48 = Resistor [tolerance=±5% resistance=10k package=THT]
  R49 = Resistor [tolerance=±5% resistance=10k package=THT]
  R50 = Resistor [tolerance=±5% resistance=10k package=THT]
  R51 = Resistor [tolerance=±5% resistance=10k package=THT]
  Q35 = PNP-Transistor [package="TO92 [THT]"]
  Q37 = NPN-Transistor [package="TO92 [THT]"]
  DPDT_Relay12 = DPDT Relay [chip_label=Relay package="DIP (Dual Inline) [THT]"]
  GND3 = female pin header, 1 pin [form="♀ (female)"]
  Out14 = female pin header, 1 pin [form="♀ (female)"]
  IN28 = female pin header, 1 pin [form="♀ (female)"]
  Out15 = female pin header, 1 pin [form="♀ (female)"]
  IN31 = female pin header, 1 pin [form="♀ (female)"]
  IN32 = female pin header, 1 pin [form="♀ (female)"]
  D12 = Rectifier Diode [part_number=1N4001 package="300 mil [THT]"]
  Q38 = NPN-Transistor [package="TO92 [THT]"]
  R52 = Resistor [tolerance=±5% resistance=10k package=THT]
  R56 = Resistor [tolerance=±5% resistance=10k package=THT]
  R57 = Resistor [tolerance=±5% resistance=10k package=THT]
  R58 = Resistor [tolerance=±5% resistance=10k package=THT]
  R59 = Resistor [tolerance=±5% resistance=10k package=THT]
  R60 = Resistor [tolerance=±5% resistance=10k package=THT]
  R61 = Resistor [tolerance=±5% resistance=10k package=THT]
  R62 = Resistor [tolerance=±5% resistance=10k package=THT]
  Out16 = female pin header, 1 pin [form="♀ (female)"]
  R63 = Resistor [tolerance=±5% resistance=10k package=THT]
  R64 = Resistor [tolerance=±5% resistance=10k package=THT]
  Out17 = female pin header, 1 pin [form="♀ (female)"]
  Out18 = female pin header, 1 pin [form="♀ (female)"]
  R65 = Resistor [tolerance=±5% resistance=10k package=THT]
  R66 = Resistor [tolerance=±5% resistance=10k package=THT]
  Out19 = female pin header, 1 pin [form="♀ (female)"]
  R67 = Resistor [tolerance=±5% resistance=10k package=THT]
  R68 = Resistor [tolerance=±5% resistance=10k package=THT]
  Out20 = female pin header, 1 pin [form="♀ (female)"]

nets:
  N1: DPDT_Relay2.pin1, DPDT_Relay4.pin1, DPDT_Relay5.pin1, DPDT_Relay6.pin1, DPDT_Relay1.pin1, D1.cathode, D2.cathode, D3.cathode, D4.cathode, D5.cathode, D6.cathode, DPDT_Relay3.pin1, J15.pin1
  N2: DPDT_Relay2.pin5, DPDT_Relay4.pin5, DPDT_Relay5.pin5, J14.pin1, DPDT_Relay1.pin5, DPDT_Relay3.pin5
  N3: DPDT_Relay2.pin6, DPDT_Relay4.pin6, DPDT_Relay5.pin6, DPDT_Relay6.pin5, DPDT_Relay1.pin6, DPDT_Relay3.pin6
  N4: DPDT_Relay2.pin7, J2.pin1, J26.pin1
  N5: DPDT_Relay2.pin8, D2.anode, Q2.C
  N6: DPDT_Relay4.pin7, J4.pin1, J20.pin1
  N7: DPDT_Relay4.pin8, D5.anode, Q4.C
  N8: DPDT_Relay5.pin7, J5.pin1, J16.pin1, R7.Pin_1, J17.pin1
  N9: DPDT_Relay5.pin8, D4.anode, Q5.C
  N10: DPDT_Relay6.pin7, J13.pin1, Q1.E, Q2.E, Q3.E, Q4.E, Q5.E, Q6.E, R8.Pin_0, R9.Pin_0, R11.Pin_0, R13.Pin_0, R15.Pin_0
  N11: DPDT_Relay6.pin8, D6.anode, Q6.C
  N12: J1.pin1, DPDT_Relay1.pin7, J29.pin1
  N13: J3.pin1, DPDT_Relay3.pin7, J23.pin1
  N14: J7.pin1, R2.Pin_0
  N15: J8.pin1, R1.Pin_0
  N16: J9.pin1, R3.Pin_0
  N17: J10.pin1, R4.Pin_0
  N18: J11.pin1, R5.Pin_0
  N19: J12.pin1, R6.Pin_0
  N20: DPDT_Relay1.pin8, D1.anode, Q1.C
  N21: D3.anode, Q3.C, DPDT_Relay3.pin8
  N22: Q1.B, R1.Pin_1
  N23: Q2.B, R2.Pin_1
  N24: Q3.B, R3.Pin_1
  N25: Q4.B, R4.Pin_1
  N26: Q5.B, R5.Pin_1
  N27: Q6.B, R6.Pin_1
  N28: J6.pin1, R7.Pin_0, R8.Pin_1
  N29: J18.pin1, R9.Pin_1, R10.Pin_0
  N30: J19.pin1, R10.Pin_1
  N31: J21.pin1, R11.Pin_1, R12.Pin_0
  N32: J22.pin1, R12.Pin_1
  N33: J24.pin1, R13.Pin_1, R14.Pin_0
  N34: J25.pin1, R14.Pin_1
  N35: J27.pin1, R15.Pin_1, R16.Pin_0
  N36: J28.pin1, R16.Pin_1
  N37: DPDT_Relay7.pin1, D7.cathode, DPDT_Relay8.pin1, D8.cathode, DPDT_Relay9.pin1, D9.cathode, 5V.pin1
  N38: DPDT_Relay7.pin2, Out.pin1
  N39: DPDT_Relay7.pin3, IN.pin1
  N40: DPDT_Relay7.pin4, Q8.C, Q10.C
  N41: DPDT_Relay7.pin5, Q11.C, Q12.C
  N42: DPDT_Relay7.pin6, IN5.pin1
  N43: DPDT_Relay7.pin7, Out1.pin1
  N44: DPDT_Relay7.pin8, D7.anode, Q13.C
  N45: Q8.E, R18.Pin_1, Q11.E, R21.Pin_1, R25.Pin_1, R30.Pin_1, Q15.E, Q16.E, R33.Pin_1, Q21.E, 12v.pin1
  N46: Q8.B, R17.Pin_0, R18.Pin_0
  N47: R17.Pin_1, IN1.pin1
  N48: Q10.E, Q12.E, Q13.E, Q14.E, Q17.E, Q18.E, Q19.E, GND.pin1
  N49: Q10.B, R19.Pin_0
  N50: R19.Pin_1, IN2.pin1
  N51: Q11.B, R20.Pin_0, R21.Pin_0
  N52: Q12.B, R22.Pin_0
  N53: R20.Pin_1, IN3.pin1
  N54: R22.Pin_1, IN4.pin1
  N55: Q13.B, R23.Pin_0
  N56: R23.Pin_1, Out2.pin1
  N57: DPDT_Relay8.pin2, Out4.pin1
  N58: DPDT_Relay8.pin3, IN9.pin1
  N59: DPDT_Relay8.pin4, Q15.C, Q17.C
  N60: DPDT_Relay8.pin5, Q16.C, Q18.C
  N61: DPDT_Relay8.pin6, IN7.pin1
  N62: DPDT_Relay8.pin7, Out3.pin1
  N63: DPDT_Relay8.pin8, D8.anode, Q14.C
  N64: IN6.pin1, R27.Pin_1
  N65: IN8.pin1, R29.Pin_1
  N66: IN10.pin1, R28.Pin_1
  N67: IN11.pin1, R26.Pin_1
  N68: Out5.pin1, R24.Pin_1
  N69: Q14.B, R24.Pin_0
  N70: R25.Pin_0, R27.Pin_0, Q15.B
  N71: R26.Pin_0, Q18.B
  N72: R28.Pin_0, Q17.B
  N73: R29.Pin_0, R30.Pin_0, Q16.B
  N74: DPDT_Relay9.pin2, Out7.pin1
  N75: DPDT_Relay9.pin3, IN14.pin1
  N76: DPDT_Relay9.pin4, Q21.C, Q22.C
  N77: DPDT_Relay9.pin8, D9.anode, Q19.C
  N78: IN13.pin1, R34.Pin_1
  N79: Out6.pin1, R37.Pin_1
  N80: IN15.pin1, R32.Pin_1
  N81: Q19.B, R37.Pin_0
  N82: R32.Pin_0, R33.Pin_0, Q21.B
  N83: R34.Pin_0, Q22.B
  N84: Q24.E, Q25.E, 12v1.pin1, R40.Pin_1, R43.Pin_1, Q29.E, Q30.E, R47.Pin_1, R50.Pin_1, Q35.E, R57.Pin_1
  N85: Q24.B, R40.Pin_0, R41.Pin_0
  N86: Q24.C, Q26.C, DPDT_Relay10.pin4
  N87: Q25.B, R43.Pin_0, R44.Pin_0
  N88: Q25.C, Q27.C, DPDT_Relay10.pin5
  N89: Q26.E, Q27.E, Q31.E, Q32.E
  N90: Q26.B, R39.Pin_0
  N91: Q27.B, R42.Pin_0
  N92: DPDT_Relay10.pin1, 5V1.pin1, D10.cathode, DPDT_Relay11.pin1, D11.cathode, DPDT_Relay12.pin1, D12.cathode
  N93: DPDT_Relay10.pin2, Out10.pin1, R61.Pin_1
  N94: DPDT_Relay10.pin3, IN21.pin1
  N95: DPDT_Relay10.pin6, IN16.pin1
  N96: DPDT_Relay10.pin7, Out9.pin1, R63.Pin_1
  N97: DPDT_Relay10.pin8, D10.anode, Q28.C
  N98: Out8.pin1, R38.Pin_1
  N99: IN17.pin1, R39.Pin_1
  N100: IN18.pin1, R41.Pin_1
  N101: IN19.pin1, R42.Pin_1
  N102: IN20.pin1, R44.Pin_1
  N103: Q28.E, Q33.E, R60.Pin_0, R64.Pin_0
  N104: Q28.B, R38.Pin_0
  N105: Q29.B, R47.Pin_0, R48.Pin_0
  N106: Q29.C, Q31.C, DPDT_Relay11.pin4
  N107: Q30.B, R50.Pin_0, R51.Pin_0
  N108: Q30.C, Q32.C, DPDT_Relay11.pin5
  N109: Q31.B, R46.Pin_0
  N110: Q32.B, R49.Pin_0
  N111: DPDT_Relay11.pin2, Out13.pin1, R65.Pin_1
  N112: DPDT_Relay11.pin3, IN27.pin1
  N113: DPDT_Relay11.pin6, IN22.pin1
  N114: DPDT_Relay11.pin7, Out12.pin1, R59.Pin_1
  N115: DPDT_Relay11.pin8, D11.anode, Q33.C
  N116: Out11.pin1, R45.Pin_1
  N117: IN23.pin1, R46.Pin_1
  N118: IN24.pin1, R48.Pin_1
  N119: IN25.pin1, R49.Pin_1
  N120: IN26.pin1, R51.Pin_1
  N121: Q33.B, R45.Pin_0
  N122: Q35.B, R57.Pin_0, R58.Pin_0
  N123: Q35.C, Q37.C, DPDT_Relay12.pin5
  N124: Q37.E, GND3.pin1, Q38.E, R62.Pin_0, R66.Pin_0, R68.Pin_0
  N125: Q37.B, R56.Pin_0
  N126: DPDT_Relay12.pin6, IN28.pin1
  N127: DPDT_Relay12.pin7, Out15.pin1, R67.Pin_1
  N128: DPDT_Relay12.pin8, D12.anode, Q38.C
  N129: Out14.pin1, R52.Pin_1
  N130: IN31.pin1, R56.Pin_1
  N131: IN32.pin1, R58.Pin_1
  N132: Q38.B, R52.Pin_0
  N133: R59.Pin_0, R62.Pin_1, Out18.pin1
  N134: R60.Pin_1, R61.Pin_0, Out16.pin1
  N135: R63.Pin_0, R64.Pin_1, Out17.pin1
  N136: R65.Pin_0, R66.Pin_1, Out19.pin1
  N137: R67.Pin_0, R68.Pin_1, Out20.pin1

custom parts:
  DPDT Relay: DIP DPDT Relay (Double Pole Double Throw)
