# Fritzing sketch OLED-HelloWorld (saved by Fritzing 0.9.3b)
breadboards: 1

parts:
  Part1 = Arduino Pro Mini v13
  J2 = Generic female header - 7 pins [form="♀ (female)" package=THT]

nets:
  GND: Part1.GND, J2.GND
  VCC: Part1.VCC, J2.VDD
  N1: Part1.D13/SCK, J2.SCK
  N2: Part1.D11_PWM/MOSI, J2.SDA
  N3: Part1.D10_PWM/SS, J2.CS
  N4: Part1.D9_PWM, J2.DC
  N5: Part1.D8, J2.RES

custom parts:
  Generic female header - 7 pins: Generic female header
